# Fritzing sketch Rocket_STAB_1 (saved by Fritzing 0.9.2b)
breadboards: 1

parts:
  Raspberry_Pi_Zero1 = Raspberry Pi Zero  # not connected
  Part1 = Adafruit BMP180
  GY1 = MPU-6050 Board GY-521 [form="♀ (female)" package=THT]
  Part2 = Adafruit ADXL377 [part_number="Adafruit #1413"]
  IC1 = ADS1115 16-bit ADC Breakout

nets:
  +5V: Part1.+5V, GY1.pin1, Part2.VIN, IC1.VDD
  GND: Part1.GND, GY1.pin2, Part2.GND, IC1.GND
  N1: Part1.SCL, GY1.pin3, IC1.SCL
  N2: Part1.SDA, GY1.pin4, IC1.SDA
  N3: Part2.ZOUT, IC1.A2
  N4: Part2.YOUT, IC1.A1
  N5: Part2.XOUT, IC1.A0

custom parts:
  Adafruit BMP180: This precision sensor from Bosch is the best low-cost sensing solution for measuring barometric pressure and temperature. Because pressure changes with altitude you can also use it as an altimeter! The sensor is soldered onto a PCB with a 3.3V regulator, I2C level shifter and pull-up resistors on the I2C pins. The BMP180 is the next-generation of sensors from Bosch, and replaces the BMP085.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
  MPU-6050 Board GY-521: Acelerometro y Giroscopio MPU-6050 Board GY-521
  Adafruit ADXL377: Hey rocket man (burnin' out your fuse out there alone) ever wonder how fast you're rocketing? The ADXL377 +-200g 3-axis accelerometer may be able to tell the answer. You read that right, this accelerometer can sense up to 200g's of force. Incredible! Not surprisingly, we couldn't say "no" to a breakout for this sensor. The sensor is soldered onto a PCB with four mounting holes (in case you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
  ADS1115 16-bit ADC Breakout: ADS1015 12-bit I2C ADC+PGA Breakout
